// Logisim project 1.circ as structural Verilog: 9 circuits, main circuit ula-8bits
module main (
  input  A,
  input  B,
  input  op,
  input  CARRY_IN,
  input  F0,
  input  F1,
  input  F2,
  output SAIDA,
  output CARRY_OUT
);

  wire DECODER_and, DECODER_nand, DECODER_nor, DECODER_not, DECODER_or, DECODER_somador, DECODER_xnor,
       DECODER_xor, logical_unit_1_and_2, logical_unit_1_nand_2, logical_unit_1_nor_2, logical_unit_1_not_2,
       logical_unit_1_or_2, logical_unit_1_sa, logical_unit_1_sb, logical_unit_1_xnor_2,
       logical_unit_1_xor_2, somador3_1_s;

  decoder DECODER (
    .F0(F0), .F1(F1), .F2(F2), .AND(DECODER_and), .OR(DECODER_or), .NOT(DECODER_not), .NAND(DECODER_nand),
    .NOR(DECODER_nor), .XOR(DECODER_xor), .XNOR(DECODER_xnor), .SOMADOR(DECODER_somador));
  logical_unit logical_unit_1 (
    .A(A), .B(B), .sA(logical_unit_1_sa), .sB(logical_unit_1_sb), .AND(DECODER_and), .OR(DECODER_or),
    .NOT(DECODER_not), .NAND(DECODER_nand), .NOR(DECODER_nor), .XOR(DECODER_xor), .XNOR(DECODER_xnor),
    .and_2(logical_unit_1_and_2), .or_2(logical_unit_1_or_2), .nand_2(logical_unit_1_nand_2),
    .not_2(logical_unit_1_not_2), .nor_2(logical_unit_1_nor_2), .xor_2(logical_unit_1_xor_2),
    .xnor_2(logical_unit_1_xnor_2));
  somador3 somador3_1 (
    .A(logical_unit_1_sa), .B(logical_unit_1_sb), .DECODER(DECODER_somador), .OP(op), .Cin(CARRY_IN),
    .CARRYOUT(CARRY_OUT), .S(somador3_1_s));
  or or_1 (SAIDA, logical_unit_1_and_2, logical_unit_1_or_2, logical_unit_1_nand_2, logical_unit_1_not_2, logical_unit_1_nor_2, logical_unit_1_xor_2, logical_unit_1_xnor_2, somador3_1_s);
endmodule

module decoder (
  input  F0,
  input  F1,
  input  F2,
  output AND,
  output OR,
  output NOT,
  output NAND,
  output NOR,
  output XOR,
  output XNOR,
  output SOMADOR
);

  wire not_1_out, not_2_out, not_3_out;

  not not_1 (not_1_out, F0);
  not not_2 (not_2_out, F1);
  not not_3 (not_3_out, F2);
  and and_1 (AND, not_1_out, not_2_out, not_3_out);
  and and_2 (OR, not_1_out, not_2_out, F2);
  and and_3 (NOT, not_1_out, F1, not_3_out);
  and and_4 (NAND, not_1_out, F1, F2);
  and and_5 (NOR, F0, not_2_out, not_3_out);
  and and_6 (XOR, F0, not_2_out, F2);
  and and_7 (XNOR, F0, F1, not_3_out);
  and and_8 (SOMADOR, F0, F1, F2);
endmodule

module logical_unit (
  input  A,
  input  B,
  input  AND,
  input  OR,
  input  NOT,
  input  NAND,
  input  NOR,
  input  XOR,
  input  XNOR,
  output and_2,
  output or_2,
  output nand_2,
  output not_2,
  output nor_2,
  output xor_2,
  output xnor_2,
  output sA,
  output sB
);

  wire and_1_out, nand_1_out, nor_1_out, not_1_out, or_1_out, xnor_1_out, xor_1_out;

  and and_1 (and_1_out, A, B);
  or or_1 (or_1_out, A, B);
  nand nand_1 (nand_1_out, A, B);
  not not_1 (not_1_out, B);
  nor nor_1 (nor_1_out, A, B);
  xor xor_1 (xor_1_out, A, B);
  xnor xnor_1 (xnor_1_out, A, B);
  and u_and_2 (and_2, and_1_out, AND);
  and and_3 (or_2, or_1_out, OR);
  and and_4 (nand_2, nand_1_out, NAND);
  and and_5 (not_2, not_1_out, NOT);
  and and_6 (nor_2, nor_1_out, NOR);
  and and_7 (xor_2, xor_1_out, XOR);
  and and_8 (xnor_2, xnor_1_out, XNOR);

  assign sA = A;
  assign sB = B;
endmodule

module ula_8bits (
  input  A7,
  input  A6,
  input  A5,
  input  A4,
  input  A3,
  input  A2,
  input  A1,
  input  A0,
  input  OP,
  input  B7,
  input  B6,
  input  B5,
  input  B4,
  input  B3,
  input  B2,
  input  B1,
  input  B0,
  input  F0,
  input  F1,
  input  F2,
  output CARRY_OUT,
  output out_22,
  output out_23,
  output out_24,
  output out_25,
  output out_26,
  output out_27,
  output out_28,
  output out_29
);

  wire main_1_carry_out, main_2_carry_out, main_3_carry_out, main_4_carry_out, main_5_carry_out,
       main_6_carry_out, main_7_carry_out;

  main main_1 (
    .F0(F0), .F1(F1), .F2(F2), .A(A0), .B(B0), .op(OP), .CARRY_IN(1'b0), .CARRY_OUT(main_1_carry_out),
    .SAIDA(out_29));
  main main_2 (
    .F0(F0), .F1(F1), .F2(F2), .A(A1), .B(B1), .op(OP), .CARRY_IN(main_1_carry_out),
    .CARRY_OUT(main_2_carry_out), .SAIDA(out_28));
  main main_3 (
    .F0(F0), .F1(F1), .F2(F2), .A(A2), .B(B2), .op(OP), .CARRY_IN(main_2_carry_out),
    .CARRY_OUT(main_3_carry_out), .SAIDA(out_27));
  main main_4 (
    .F0(F0), .F1(F1), .F2(F2), .A(A3), .B(B3), .op(OP), .CARRY_IN(main_3_carry_out),
    .CARRY_OUT(main_4_carry_out), .SAIDA(out_26));
  main main_5 (
    .F0(F0), .F1(F1), .F2(F2), .A(A4), .B(B4), .op(OP), .CARRY_IN(main_4_carry_out),
    .CARRY_OUT(main_5_carry_out), .SAIDA(out_25));
  main main_6 (
    .F0(F0), .F1(F1), .F2(F2), .A(A5), .B(B5), .op(OP), .CARRY_IN(main_5_carry_out),
    .CARRY_OUT(main_6_carry_out), .SAIDA(out_24));
  main main_7 (
    .F0(F0), .F1(F1), .F2(F2), .A(A6), .B(B6), .op(OP), .CARRY_IN(main_6_carry_out),
    .CARRY_OUT(main_7_carry_out), .SAIDA(out_23));
  main main_8 (
    .F0(F0), .F1(F1), .F2(F2), .A(A7), .B(B7), .op(OP), .CARRY_IN(main_7_carry_out), .CARRY_OUT(CARRY_OUT),
    .SAIDA(out_22));

  // Notes on the sheet:
  //   000 – AND | 001  OR | 010 – NOT B  |  011 – NAND  |  100 - NOR  |  101 - XOR  |  110 -  XNOR |  111 - SOMADOR\
endmodule

module somador3 (
  input  A,
  input  B,
  input  OP,
  input  Cin,
  input  DECODER,
  output S,
  output CARRYOUT
);

  wire and_1_out, and_2_out, and_3_out, and_4_out, and_5_out, and_6_out, and_7_out, and_8_out, and_9_out,
       not_1_out, not_2_out, not_3_out, not_4_out, not_5_out, not_6_out, not_7_out, not_8_out, not_9_out,
       not_10_out, not_11_out, not_12_out;

  not not_1 (not_1_out, A);
  not not_2 (not_2_out, B);
  not not_3 (not_3_out, OP);
  not not_4 (not_4_out, A);
  not not_5 (not_5_out, Cin);
  not not_6 (not_6_out, B);
  not not_7 (not_7_out, Cin);
  not not_8 (not_8_out, OP);
  not not_9 (not_9_out, OP);
  not not_10 (not_10_out, OP);
  not not_11 (not_11_out, Cin);
  not not_12 (not_12_out, A);
  and and_1 (and_1_out, not_1_out, not_2_out, not_3_out, Cin, DECODER);
  and and_2 (and_2_out, not_4_out, B, not_5_out, DECODER);
  and and_3 (and_3_out, A, not_6_out, not_7_out, DECODER);
  and and_4 (and_4_out, A, B, Cin, DECODER);
  and and_5 (and_5_out, not_8_out, A, B, DECODER);
  and and_6 (and_6_out, not_9_out, Cin, B, DECODER);
  and and_7 (and_7_out, not_10_out, Cin, A, DECODER);
  and and_8 (and_8_out, Cin, A, B);
  and and_9 (and_9_out, OP, not_11_out, not_12_out, B);
  or or_1 (S, and_1_out, and_2_out, and_3_out, and_4_out);
  or or_2 (CARRYOUT, and_5_out, and_6_out, and_7_out, and_8_out, and_9_out);
endmodule

module teste (
  input  in_1,
  input  in_2,
  input  in_3,
  input  in_4,
  input  in_5,
  input  in_6,
  input  in_7,
  input  in_8
);

  centena centena_1 (.in_1(in_1), .in_2(in_2), .in_3(in_3), .in_4(in_5), .in_5(in_6));

  // Notes on the sheet:
  //   128
endmodule

module centena (
  input  in_1,
  input  in_2,
  input  in_3,
  input  in_4,
  input  in_5
);
endmodule

module splitter (
  input  A7,
  input  A6,
  input  A5,
  input  A4,
  input  A3,
  input  A2,
  input  A1,
  input  A0,
  input  [7:0] _100,
  input  [7:0] _100_2,
  output D,
  output C,
  output B,
  output A,
  output D_2,
  output C_2,
  output B_2,
  output A_2
);

  wire display_1_a_2, display_1_b_2, display_1_c_2, display_1_d_2, display_1_e, display_1_f, display_1_g;
  wire [7:0] divider_1_out, divider_1_rem;
  wire [7:4] divider_2_out, divider_2_rem;

  Divider divider_1 (
    .a({A7, A6, A5, A4, A3, A2, A1, A0}), .b(_100), .out(divider_1_out), .rem(divider_1_rem));  // open: upper
  Divider divider_2 (
    .a(divider_1_rem), .b(_100_2), .out({divider_2_out, A, B, C, D}),
    .rem({divider_2_rem, A_2, B_2, C_2, D_2}));  // open: upper
  DISPLAY display_1 (
    .A(divider_1_out[0]), .B(divider_1_out[1]), .C(divider_1_out[2]), .D(divider_1_out[3]),
    .A_2(display_1_a_2), .B_2(display_1_b_2), .C_2(display_1_c_2), .D_2(display_1_d_2), .E(display_1_e),
    .F(display_1_f), .G(display_1_g));
  _7_Segment_Display u_7_segment_display_1 (
    .g(display_1_g), .f(display_1_f), .a(display_1_a_2), .b(display_1_b_2), .e(display_1_e),
    .d(display_1_d_2), .c(display_1_c_2));  // open: dp
endmodule

module DISPLAY (
  input  A,
  input  B,
  input  C,
  input  D,
  output A_2,
  output B_2,
  output C_2,
  output D_2,
  output E,
  output F,
  output G
);

  wire and_1_out, and_2_out, and_3_out, and_4_out, and_5_out, and_6_out, and_7_out, and_8_out, and_9_out,
       and_10_out, and_11_out, and_12_out, and_13_out, and_14_out, and_15_out, not_1_out, not_2_out,
       not_3_out, not_4_out, or_1_out, or_2_out, or_3_out, or_4_out, or_5_out, xnor_1_out;

  not not_1 (not_1_out, A);
  not not_2 (not_2_out, B);
  not not_3 (not_3_out, C);
  not not_4 (not_4_out, D);
  or or_1 (or_1_out, not_1_out, and_1_out);
  and and_1 (and_1_out, not_3_out, not_4_out);
  and and_2 (and_2_out, B, or_1_out);
  and and_3 (and_3_out, not_2_out, C);
  or u_G (G, and_2_out, and_3_out, D);
  and and_4 (and_4_out, not_1_out, B);
  or or_2 (or_2_out, and_4_out, not_2_out);
  and and_5 (and_5_out, or_2_out, C);
  and and_6 (and_6_out, not_2_out, not_1_out);
  or u_F (F, and_5_out, and_6_out, D);
  and and_7 (and_7_out, B, not_1_out);
  and and_8 (and_8_out, not_3_out, not_1_out);
  or u_E (E, and_7_out, and_8_out);
  and and_9 (and_9_out, not_4_out, not_3_out);
  or or_3 (or_3_out, and_9_out, not_1_out);
  and and_10 (and_10_out, or_3_out, B);
  and and_11 (and_11_out, not_1_out, not_3_out);
  and and_12 (and_12_out, C, B, A);
  or u_D (D_2, and_10_out, and_11_out, and_12_out);
  or or_4 (or_4_out, C, A);
  and and_13 (and_13_out, or_4_out, not_4_out);
  or u_C (C_2, and_13_out, not_2_out, D);
  or or_5 (or_5_out, D, C);
  and and_14 (and_14_out, not_3_out, not_4_out);
  and and_15 (and_15_out, not_2_out, not_1_out);
  or u_B (B_2, or_5_out, and_14_out, and_15_out, A);
  xnor xnor_1 (xnor_1_out, C, A);
  or u_A (A_2, xnor_1_out, B, D);
endmodule
